// Logisim project pricssor1.circ as structural Verilog: 19 circuits, main circuit PRICSSOR1
module PRICSSOR1 (
  input  [15:0] SYS_IN_IN,
  input  RET_IN,
  input  CLK,
  input  CLR,
  output [15:0] SYS_OUT0,
  output [15:0] SYS_OUT1,
  output [15:0] SYS_OUT2,
  output [15:0] SYS_OUT3,
  output [15:0] SYS_OUT4,
  output [15:0] SYS_OUT5,
  output [15:0] SYS_OUT6,
  output [15:0] SYS_OUT7,
  output [15:0] SYS_PRT,
  output PNG,
  output PUT,
  output HLT
);

  wire ADD, CME, CMF, CMG, CML, CMN, CMT, DIV, FLG, GET, LOD_A, LOD_B, LOD_FLG, LOD_INS, LOD_SYS_IN, LOG_AND,
       LOG_LOR, LOG_NOT, LOG_XOR, MOV, MUL, MVA, MVB, MVG, MVI, POP, PSH, RET, STR_A, STR_B, STR_FLG,
       STR_INS, STR_SYS_IN, SUB;
  wire [2:0] DTAX_ADR, DTAY_ADR, DTAZ_ADR, SYS_OUT_ADR;
  wire [7:0] INS_ADR;

  CTL ctl_1 (
    .FLG(FLG), .RET(RET), .CLK(CLK), .CLR(CLR), .INS(SYS_PRT), .LOD_FLG(LOD_FLG), .VAL(SYS_PRT),
    .SYS_IO_ADR(SYS_OUT_ADR), .HLT(HLT), .GET(GET), .PUT(PUT), .STR_SYS_IN(STR_SYS_IN), .MVG(MVG),
    .LOD_SYS_IN(LOD_SYS_IN), .STR_INS(STR_INS), .PSH(PSH), .POP(POP), .PNG(PNG), .DTAY_ADR(DTAY_ADR),
    .DTAZ_ADR(DTAZ_ADR), .DTAX_ADR(DTAX_ADR), .XOR_OP(LOG_XOR), .STR_A(STR_A), .STR_B(STR_B), .CME_OP(CME),
    .CMN_OP(CMN), .CML_OP(CML), .CMG_OP(CMG), .CMF_OP(CMF), .CMT_OP(CMT), .MVI(MVI), .MOV_OP(MOV),
    .LOD_A(LOD_A), .LOD_B(LOD_B), .STR_FLG(STR_FLG), .ADD(ADD), .SUB(SUB), .MUL(MUL), .DIV(DIV),
    .NOT_OP(LOG_NOT), .AND_OP(LOG_AND), .LOR_OP(LOG_LOR), .MVA(MVA), .MVB(MVB), .LOD_INS(LOD_INS),
    .INS_ADR(INS_ADR));
  CMP cmp_1 (
    .EQ_OP(CME), .NQ_OP(CMN), .LT_OP(CML), .GT_OP(CMG), .TRU_OP(CMT), .FLS_OP(CMF), .CLK(CLK), .CLR(CLR),
    .STR_A(STR_A), .LOD_A(LOD_A), .STR_B(STR_B), .LOD_B(LOD_B), .STR_FLG(STR_FLG), .LOD_FLG(LOD_FLG),
    .LOG_IN(SYS_PRT), .FLG(FLG));
  SYS_IN sys_in_1 (
    .SYS_IN_IN(SYS_IN_IN), .STR_SYS_IN(STR_SYS_IN), .LOD_SYS_IN(LOD_SYS_IN), .CLK(CLK), .CLR(CLR),
    .RET_IN(RET_IN), .RET(RET), .SYS_IN_OUT(SYS_PRT));
  MEM mem_1 (
    .POP(POP), .MVG(MVG), .DTAX_ADR(DTAX_ADR), .DTAY_ADR(DTAY_ADR), .DTAZ_ADR(DTAZ_ADR), .MVA(MVA),
    .MVB(MVB), .MOV_OP(MOV), .MUL_OP(MUL), .DIV_OP(DIV), .PUT(PUT), .ADD_OP(ADD), .SUB_OP(SUB),
    .NOT_OP(LOG_NOT), .AND_OP(LOG_AND), .LOR_OP(LOG_LOR), .XOR_OP(LOG_XOR), .PSH(PSH), .LOD_INS(LOD_INS),
    .STR_INS(STR_INS), .INS_ADR(INS_ADR), .INS_IN(SYS_PRT), .MVI(MVI), .DTA_IN(SYS_PRT), .CLK(CLK),
    .CLR(CLR), .DTA_OUT(SYS_PRT), .INS(SYS_PRT));
  SYS_OUT sys_out_1 (
    .PUT(PUT), .SYS_OUT_ADR(SYS_OUT_ADR), .CLK(CLK), .CLR(CLR), .SYS_OUT_IN(SYS_PRT), .SYS_OUT0(SYS_OUT0),
    .SYS_OUT1(SYS_OUT1), .SYS_OUT2(SYS_OUT2), .SYS_OUT3(SYS_OUT3), .SYS_OUT4(SYS_OUT4), .SYS_OUT5(SYS_OUT5),
    .SYS_OUT6(SYS_OUT6), .SYS_OUT7(SYS_OUT7));
  STK stk_1 (.CLK(CLK), .POP(POP), .CLR(CLR), .PSH(PSH), .STK_ADR(INS_ADR));

  // Other names for the same wires on the sheet: BUS_W[15:0] = SYS_PRT
endmodule

module MEM (
  input  [2:0] DTAX_ADR,
  input  [7:0] INS_ADR,
  input  LOD_INS,
  input  STR_INS,
  input  [15:0] INS_IN,
  input  [2:0] DTAY_ADR,
  input  [15:0] DTA_IN,
  input  CLK,
  input  CLR,
  input  [2:0] DTAZ_ADR,
  input  POP,
  input  MVG,
  input  MOV_OP,
  input  ADD_OP,
  input  SUB_OP,
  input  MUL_OP,
  input  DIV_OP,
  input  NOT_OP,
  input  MVI,
  input  AND_OP,
  input  LOR_OP,
  input  XOR_OP,
  input  PSH,
  input  PUT,
  input  MVA,
  input  MVB,
  output [15:0] INS,
  output [15:0] DTA_OUT
);

  wire ARI_LOG, LOD_DTA0_X, LOD_DTA0_Y, LOD_DTA1_X, LOD_DTA1_Y, LOD_DTA2_X, LOD_DTA2_Y, LOD_DTA3_X,
       LOD_DTA3_Y, LOD_DTA4_X, LOD_DTA4_Y, LOD_DTA5_X, LOD_DTA5_Y, LOD_DTA6_X, LOD_DTA6_Y, LOD_DTA7_X,
       LOD_DTA7_Y, MVAB, or_1_out, or_2_out, or_3_out, or_4_out, or_5_out, or_6_out, or_7_out, or_8_out,
       or_10_out, or_11_out, STR_DTA0_Z, STR_DTA1_Z, STR_DTA2_Z, STR_DTA3_Z, STR_DTA4_Z, STR_DTA5_Z,
       STR_DTA6_Z, STR_DTA7_Z;
  wire [15:0] adder_1_out, and_1_out, divider_1_out, DTA0_OUT, DTA1_OUT, DTA2_OUT, DTA3_OUT, DTA4_OUT,
       DTA5_OUT, DTA6_OUT, DTA7_OUT, multiplexer_1_out, multiplexer_2_out, multiplier_1_out, not_1_out,
       or_12_out, ram_1_dout, subtractor_1_out, xor_1_out;

  or or_1 (or_1_out, LOD_DTA0_X, LOD_DTA0_Y);
  or or_2 (or_2_out, LOD_DTA1_X, LOD_DTA1_Y);
  or or_3 (or_3_out, LOD_DTA2_X, LOD_DTA2_Y);
  or or_4 (or_4_out, LOD_DTA3_X, LOD_DTA3_Y);
  or or_5 (or_5_out, LOD_DTA4_X, LOD_DTA4_Y);
  or or_6 (or_6_out, LOD_DTA5_X, LOD_DTA5_Y);
  or or_7 (or_7_out, LOD_DTA6_X, LOD_DTA6_Y);
  or or_8 (or_8_out, LOD_DTA7_X, LOD_DTA7_Y);
  RAM #(.dataWidth(16), .enables("line")) ram_1 (
    .addr(INS_ADR), .we(STR_INS), .clk(CLK), .din(INS_IN), .dout(ram_1_dout));
  REG16 reg16_1 (.REG_IN(DTA_IN), .STR(STR_DTA0_Z), .LOD(or_1_out), .CLK(CLK), .CLR(CLR), .REG_OUT(DTA0_OUT));
  REG16 reg16_2 (.REG_IN(DTA_IN), .STR(STR_DTA1_Z), .LOD(or_2_out), .CLK(CLK), .CLR(CLR), .REG_OUT(DTA1_OUT));
  REG16 reg16_3 (.REG_IN(DTA_IN), .STR(STR_DTA2_Z), .LOD(or_3_out), .CLK(CLK), .CLR(CLR), .REG_OUT(DTA2_OUT));
  REG16 reg16_4 (.REG_IN(DTA_IN), .STR(STR_DTA3_Z), .LOD(or_4_out), .CLK(CLK), .CLR(CLR), .REG_OUT(DTA3_OUT));
  REG16 reg16_5 (.REG_IN(DTA_IN), .STR(STR_DTA4_Z), .LOD(or_5_out), .CLK(CLK), .CLR(CLR), .REG_OUT(DTA4_OUT));
  REG16 reg16_6 (.REG_IN(DTA_IN), .STR(STR_DTA5_Z), .LOD(or_6_out), .CLK(CLK), .CLR(CLR), .REG_OUT(DTA5_OUT));
  REG16 reg16_7 (.REG_IN(DTA_IN), .STR(STR_DTA6_Z), .LOD(or_7_out), .CLK(CLK), .CLR(CLR), .REG_OUT(DTA6_OUT));
  REG16 reg16_8 (.REG_IN(DTA_IN), .STR(STR_DTA7_Z), .LOD(or_8_out), .CLK(CLK), .CLR(CLR), .REG_OUT(DTA7_OUT));
  assign INS = LOD_INS ? ram_1_dout : 16'bz;  // Controlled_Buffer controlled_buffer_1
  or or_9 (ARI_LOG, MVI, MOV_OP, ADD_OP, SUB_OP, MUL_OP, DIV_OP, NOT_OP, AND_OP, LOR_OP, XOR_OP);
  Multiplexer #(.select(3), .width(16)) multiplexer_1 (
    .in0(DTA0_OUT), .in1(DTA1_OUT), .in2(DTA2_OUT), .in3(DTA3_OUT), .in4(DTA4_OUT), .in5(DTA5_OUT),
    .in6(DTA6_OUT), .in7(DTA7_OUT), .out(multiplexer_1_out), .sel(DTAX_ADR));
  Multiplexer #(.select(3), .width(16)) multiplexer_2 (
    .in0(DTA0_OUT), .in1(DTA1_OUT), .in2(DTA2_OUT), .in3(DTA3_OUT), .in4(DTA4_OUT), .in5(DTA5_OUT),
    .in6(DTA6_OUT), .in7(DTA7_OUT), .out(multiplexer_2_out), .sel(DTAY_ADR));
  Decoder #(.select(3)) decoder_1 (
    .out0(LOD_DTA0_X), .out1(LOD_DTA1_X), .out2(LOD_DTA2_X), .out3(LOD_DTA3_X), .out4(LOD_DTA4_X),
    .out5(LOD_DTA5_X), .out6(LOD_DTA6_X), .out7(LOD_DTA7_X), .sel(DTAX_ADR), .en(or_10_out));
  or or_10 (or_10_out, ARI_LOG, PSH, PUT, MVAB);
  Decoder #(.select(3)) decoder_2 (
    .out0(LOD_DTA0_Y), .out1(LOD_DTA1_Y), .out2(LOD_DTA2_Y), .out3(LOD_DTA3_Y), .out4(LOD_DTA4_Y),
    .out5(LOD_DTA5_Y), .out6(LOD_DTA6_Y), .out7(LOD_DTA7_Y), .sel(DTAY_ADR), .en(ARI_LOG));
  Decoder #(.select(3)) decoder_3 (
    .out0(STR_DTA0_Z), .out1(STR_DTA1_Z), .out2(STR_DTA2_Z), .out3(STR_DTA3_Z), .out4(STR_DTA4_Z),
    .out5(STR_DTA5_Z), .out6(STR_DTA6_Z), .out7(STR_DTA7_Z), .sel(DTAZ_ADR), .en(or_11_out));
  or or_11 (or_11_out, ARI_LOG, POP, MVG);
  Adder #(.width(16)) adder_1 (.a(multiplexer_1_out), .b(multiplexer_2_out), .out(adder_1_out));  // open: cin, cout
  Subtractor #(.width(16)) subtractor_1 (
    .a(multiplexer_1_out), .b(multiplexer_2_out), .out(subtractor_1_out));  // open: bin, bout
  Multiplier #(.width(16)) multiplier_1 (
    .a(multiplexer_1_out), .b(multiplexer_2_out), .out(multiplier_1_out));  // open: cin, cout
  Divider #(.width(16)) divider_1 (
    .a(multiplexer_1_out), .b(multiplexer_2_out), .out(divider_1_out));  // open: upper, rem
  assign not_1_out = ~multiplexer_1_out;  // NOT_Gate not_1, 16 bits wide
  assign and_1_out = multiplexer_1_out & multiplexer_2_out;  // AND_Gate and_1, 16 bits wide
  assign or_12_out = multiplexer_1_out | multiplexer_2_out;  // OR_Gate or_12, 16 bits wide
  assign xor_1_out = multiplexer_1_out ^ multiplexer_2_out;  // XOR_Gate xor_1, 16 bits wide
  assign DTA_OUT = MOV_OP ? multiplexer_1_out : 16'bz;  // Controlled_Buffer controlled_buffer_2
  assign DTA_OUT = ADD_OP ? adder_1_out : 16'bz;  // Controlled_Buffer controlled_buffer_3
  assign DTA_OUT = SUB_OP ? subtractor_1_out : 16'bz;  // Controlled_Buffer controlled_buffer_4
  assign DTA_OUT = MUL_OP ? multiplier_1_out : 16'bz;  // Controlled_Buffer controlled_buffer_5
  assign DTA_OUT = DIV_OP ? divider_1_out : 16'bz;  // Controlled_Buffer controlled_buffer_6
  assign DTA_OUT = NOT_OP ? not_1_out : 16'bz;  // Controlled_Buffer controlled_buffer_7
  assign DTA_OUT = AND_OP ? and_1_out : 16'bz;  // Controlled_Buffer controlled_buffer_8
  assign DTA_OUT = LOR_OP ? or_12_out : 16'bz;  // Controlled_Buffer controlled_buffer_9
  assign DTA_OUT = XOR_OP ? xor_1_out : 16'bz;  // Controlled_Buffer controlled_buffer_10
  assign DTA_OUT = PSH ? multiplexer_1_out : 16'bz;  // Controlled_Buffer controlled_buffer_11
  assign DTA_OUT = PUT ? multiplexer_1_out : 16'bz;  // Controlled_Buffer controlled_buffer_12
  assign DTA_OUT = MVAB ? multiplexer_1_out : 16'bz;  // Controlled_Buffer controlled_buffer_13
  or or_13 (MVAB, MVA, MVB);

  // Other names for the same wires on the sheet: ADD = ADD_OP; DIV = DIV_OP; MOV = MOV_OP; MUL = MUL_OP; SUB = SUB_OP
endmodule

module CMP (
  input  [15:0] LOG_IN,
  input  CLK,
  input  CLR,
  input  STR_A,
  input  LOD_A,
  input  EQ_OP,
  input  STR_B,
  input  NQ_OP,
  input  LOD_B,
  input  LT_OP,
  input  GT_OP,
  input  STR_FLG,
  input  LOD_FLG,
  input  FLS_OP,
  input  TRU_OP,
  output FLG
);

  wire and_1_out, and_2_out, and_3_out, comparator_1_eq, comparator_1_gt, comparator_1_lt,
       controlled_buffer_1_out, not_1_out, not_2_out, not_3_out, not_4_out, not_5_out, not_6_out, not_7_out,
       not_8_out, not_9_out, not_10_out, not_11_out, not_12_out, not_13_out, not_14_out, not_15_out,
       not_16_out, not_17_out;
  wire [15:0] FLG_IN, reg16_1_reg_out, reg16_2_reg_out;
  wire [15:1] reg16_3_reg_out;

  REG16 reg16_1 (.REG_IN(LOG_IN), .STR(STR_A), .LOD(LOD_A), .CLK(CLK), .CLR(CLR), .REG_OUT(reg16_1_reg_out));
  REG16 reg16_2 (.REG_IN(LOG_IN), .STR(STR_B), .LOD(LOD_B), .CLK(CLK), .CLR(CLR), .REG_OUT(reg16_2_reg_out));
  REG16 reg16_3 (.REG_IN(FLG_IN), .STR(STR_FLG), .LOD(LOD_FLG), .CLK(CLK), .CLR(CLR), .REG_OUT({reg16_3_reg_out, FLG}));
  Comparator #(.width(16)) comparator_1 (
    .a(reg16_1_reg_out), .b(reg16_2_reg_out), .gt(comparator_1_gt), .eq(comparator_1_eq), .lt(comparator_1_lt));
  not not_1 (not_1_out, reg16_1_reg_out[1]);
  not not_2 (not_2_out, reg16_1_reg_out[2]);
  not not_3 (not_3_out, reg16_1_reg_out[3]);
  not not_4 (not_4_out, reg16_1_reg_out[4]);
  not not_5 (not_5_out, reg16_1_reg_out[5]);
  not not_6 (not_6_out, reg16_1_reg_out[6]);
  not not_7 (not_7_out, reg16_1_reg_out[7]);
  not not_8 (not_8_out, reg16_1_reg_out[8]);
  not not_9 (not_9_out, reg16_1_reg_out[9]);
  not not_10 (not_10_out, reg16_1_reg_out[10]);
  not not_11 (not_11_out, reg16_1_reg_out[11]);
  not not_12 (not_12_out, reg16_1_reg_out[12]);
  not not_13 (not_13_out, reg16_1_reg_out[13]);
  not not_14 (not_14_out, reg16_1_reg_out[14]);
  not not_15 (not_15_out, reg16_1_reg_out[15]);
  not not_16 (not_16_out, comparator_1_eq);
  and and_1 (and_1_out, not_1_out, not_2_out, not_3_out, not_4_out, not_5_out, not_6_out, not_7_out, not_8_out, not_9_out, not_10_out, not_11_out, not_12_out, not_13_out, not_14_out, not_15_out);
  assign controlled_buffer_1_out = EQ_OP ? comparator_1_eq : 1'bz;  // Controlled_Buffer controlled_buffer_1
  assign controlled_buffer_1_out = NQ_OP ? not_16_out : 1'bz;  // Controlled_Buffer controlled_buffer_2
  assign controlled_buffer_1_out = LT_OP ? comparator_1_lt : 1'bz;  // Controlled_Buffer controlled_buffer_3
  assign controlled_buffer_1_out = GT_OP ? comparator_1_gt : 1'bz;  // Controlled_Buffer controlled_buffer_4
  not not_17 (not_17_out, reg16_1_reg_out[0]);
  and and_2 (and_2_out, not_17_out, and_1_out);
  and and_3 (and_3_out, reg16_1_reg_out[0], and_1_out);
  assign controlled_buffer_1_out = FLS_OP ? and_2_out : 1'bz;  // Controlled_Buffer controlled_buffer_5
  assign controlled_buffer_1_out = TRU_OP ? and_3_out : 1'bz;  // Controlled_Buffer controlled_buffer_6
  assign FLG_IN = {{15{1'b0}}, controlled_buffer_1_out};  // Bit_Extender bit_extender_1
endmodule

module CTL (
  input  CLK,
  input  CLR,
  input  RET,
  input  [15:0] INS,
  input  FLG,
  output HLT,
  output LOD_INS,
  output [7:0] INS_ADR,
  output MVI,
  output MOV_OP,
  output LOD_FLG,
  output GET,
  output PSH,
  output LOD_A,
  output PUT,
  output POP,
  output LOD_B,
  output STR_INS,
  output STR_FLG,
  output STR_SYS_IN,
  output ADD,
  output SUB,
  output PNG,
  output MUL,
  output DIV,
  output NOT_OP,
  output AND_OP,
  output LOR_OP,
  output LOD_SYS_IN,
  output XOR_OP,
  output STR_A,
  output MVG,
  output STR_B,
  output MVA,
  output MVB,
  output CME_OP,
  output [15:0] VAL,
  output CMN_OP,
  output CML_OP,
  output CMG_OP,
  output CMF_OP,
  output CMT_OP,
  output [2:0] DTAZ_ADR,
  output [2:0] SYS_IO_ADR,
  output [2:0] DTAX_ADR,
  output [2:0] DTAY_ADR
);

  wire and_1_out, and_3_out, and_4_out, and_5_out, and_6_out, and_8_out, and_9_out, and_12_out, and_13_out,
       and_14_out, ARI, CLK_t, CMP, DEC, decoder_9_out1, decoder_9_out2, EXE, FET, GET_t, INT, IO, JMF, JMP,
       JMP_OP, JMT, MOV, MOV_MVI, MVAB, MVG_t, MVI_t, nand_1_out, not_1_out, not_2_out, not_3_out, not_4_out,
       not_5_out, not_6_out, not_7_out, not_8_out, not_9_out, not_10_out, or_1_out, or_2_out, or_3_out,
       or_4_out, or_5_out, or_6_out, or_7_out, PNG_t, POP_t, PSH_t, PUT_t, STK, SYS;
  wire [1:0] FDE_q;
  wire [15:0] bit_extender_1_out, IR_OUT, multiplexer_1_out, multiplexer_2_out, PC_pc_out;
  wire [15:8] IAR_reg_out;

  not not_1 (not_1_out, HLT);
  or or_1 (or_1_out, JMP, JMF, JMT);
  and and_1 (and_1_out, CLK, not_1_out);
  nand nand_1 (nand_1_out, DEC, INT);
  or or_2 (or_2_out, or_1_out, DEC);
  or or_3 (or_3_out, EXE, SYS);
  and and_2 (CLK_t, and_1_out, nand_1_out);
  Decoder #(.select(4)) decoder_1 (
    .out1(MOV_MVI), .out2(ARI), .out3(MVAB), .out4(CMP), .out5(JMP_OP), .out6(IO), .out7(MVG_t), .out8(STK),
    .out9(PNG_t), .sel(IR_OUT[15:12]), .en(EXE));  // open: out0, out10, out11, out12, out13, out14, out15
  Decoder decoder_2 (.out0(MOV), .out1(MVI_t), .sel(IR_OUT[11]), .en(MOV_MVI));
  Decoder decoder_3 (.out0(GET_t), .out1(PUT_t), .sel(IR_OUT[11]), .en(IO));
  Decoder decoder_4 (.out0(POP_t), .out1(PSH_t), .sel(IR_OUT[11]), .en(STK));
  Counter #(.max('h3), .trigger("falling"), .width(2)) FDE (
    .Q(FDE_q), .clk(CLK_t), .clr(CLR));  // open: load, D, count, carry, up
  Decoder #(.select(2)) decoder_5 (.out0(FET), .out1(DEC), .out2(EXE), .out3(SYS), .sel(FDE_q));  // open: en
  PC16 PC (
    .PC_IN(IR_OUT[7:0]), .STR_PC(or_1_out), .LOD_PC(FET), .EN_PC(or_2_out), .CLK(CLK_t), .CLR(CLR),
    .PC_OUT(PC_pc_out));
  REG16 IR (.REG_IN(INS), .STR(DEC), .LOD(or_3_out), .CLK(CLK_t), .CLR(CLR), .REG_OUT(IR_OUT));
  or or_4 (or_4_out, DEC, POP_t);
  REG16 IAR (.REG_IN(PC_pc_out), .STR(FET), .LOD(DEC), .CLK(CLK_t), .CLR(CLR), .REG_OUT({IAR_reg_out, INS_ADR}));
  Decoder #(.disabled("Z"), .select(3)) decoder_6 (
    .out0(ADD), .out1(SUB), .out2(MUL), .out3(DIV), .out4(NOT_OP), .out5(AND_OP), .out6(LOR_OP),
    .out7(XOR_OP), .sel({IR_OUT[11], IR_OUT[7], IR_OUT[3]}), .en(and_3_out));
  and and_3 (and_3_out, EXE, ARI);
  and and_4 (and_4_out, EXE, MVAB);
  Decoder #(.disabled("Z")) decoder_7 (.out0(MVA), .out1(MVB), .sel(IR_OUT[8]), .en(and_4_out));
  and and_5 (and_5_out, EXE, CMP);
  Decoder #(.disabled("Z"), .select(4)) decoder_8 (
    .out0(CME_OP), .out1(CMN_OP), .out2(CML_OP), .out3(CMG_OP), .out4(CMF_OP), .out5(CMT_OP),
    .sel(IR_OUT[11:8]), .en(and_5_out));  // open: out6, out7, out8, out9, out10, out11, out12, out13, out14, out15
  or or_5 (or_5_out, MOV_MVI, ARI, MVG_t, POP_t);
  or or_6 (or_6_out, MOV, MVAB, PSH_t, ARI, PUT_t);
  assign DTAY_ADR = ARI ? IR_OUT[2:0] : 3'bz;  // Controlled_Buffer controlled_buffer_1
  assign LOD_INS = or_4_out ? or_4_out : 1'bz;  // Controlled_Buffer controlled_buffer_2
  assign MVI = MVI_t ? MVI_t : 1'bz;  // Controlled_Buffer controlled_buffer_3
  assign MOV_OP = MOV ? MOV : 1'bz;  // Controlled_Buffer controlled_buffer_4
  assign LOD_A = CMP ? CMP : 1'bz;  // Controlled_Buffer controlled_buffer_5
  assign LOD_B = CMP ? CMP : 1'bz;  // Controlled_Buffer controlled_buffer_6
  assign STR_FLG = CMP ? CMP : 1'bz;  // Controlled_Buffer controlled_buffer_7
  assign DTAZ_ADR = or_5_out ? IR_OUT[10:8] : 3'bz;  // Controlled_Buffer controlled_buffer_8
  assign DTAX_ADR = or_6_out ? IR_OUT[6:4] : 3'bz;  // Controlled_Buffer controlled_buffer_9
  Multiplexer #(.width(16)) multiplexer_1 (.in0({16{1'b0}}), .in1(IR_OUT), .out(multiplexer_1_out), .sel(EXE));
  Multiplexer #(.width(16)) multiplexer_2 (.in0({16{1'b0}}), .in1(IR_OUT), .out(multiplexer_2_out), .sel(SYS));
  assign LOD_FLG = JMP_OP ? JMP_OP : 1'bz;  // Controlled_Buffer controlled_buffer_10
  and and_6 (and_6_out, EXE, JMP_OP);
  Decoder #(.select(2)) decoder_9 (
    .out0(JMP), .out1(decoder_9_out1), .out2(decoder_9_out2), .sel(IR_OUT[9:8]), .en(and_6_out));  // open: out3
  assign bit_extender_1_out = {{8{1'b0}}, IR_OUT[7:0]};  // Bit_Extender bit_extender_1
  or or_7 (or_7_out, MVI_t, PNG_t);
  and and_7 (HLT, multiplexer_1_out[0], multiplexer_1_out[1], multiplexer_1_out[2], multiplexer_1_out[3], multiplexer_1_out[4], multiplexer_1_out[5], multiplexer_1_out[6], multiplexer_1_out[7], multiplexer_1_out[8], multiplexer_1_out[9], multiplexer_1_out[10], multiplexer_1_out[11], multiplexer_1_out[12], multiplexer_1_out[13], multiplexer_1_out[14], multiplexer_1_out[15]);
  and and_8 (and_8_out, multiplexer_2_out[0], multiplexer_2_out[1], multiplexer_2_out[2], multiplexer_2_out[3]);
  not not_2 (not_2_out, multiplexer_2_out[4]);
  not not_3 (not_3_out, multiplexer_2_out[5]);
  not not_4 (not_4_out, multiplexer_2_out[6]);
  not not_5 (not_5_out, multiplexer_2_out[7]);
  and and_9 (and_9_out, multiplexer_2_out[8], multiplexer_2_out[9], multiplexer_2_out[10], multiplexer_2_out[11]);
  not not_6 (not_6_out, multiplexer_2_out[12]);
  not not_7 (not_7_out, multiplexer_2_out[13]);
  not not_8 (not_8_out, multiplexer_2_out[14]);
  not not_9 (not_9_out, multiplexer_2_out[15]);
  and and_10 (JMF, decoder_9_out1, not_10_out);
  not not_10 (not_10_out, FLG);
  and and_11 (JMT, FLG, decoder_9_out2);
  assign VAL = or_7_out ? bit_extender_1_out : 16'bz;  // Controlled_Buffer controlled_buffer_11
  assign SYS_IO_ADR = PUT_t ? IR_OUT[10:8] : 3'bz;  // Controlled_Buffer controlled_buffer_12
  and and_12 (and_12_out, not_2_out, not_3_out, not_4_out, not_5_out);
  and and_13 (and_13_out, not_6_out, not_7_out, not_8_out, not_9_out);
  and and_14 (and_14_out, and_8_out, and_12_out, and_9_out, and_13_out);
  assign GET = GET_t ? GET_t : 1'bz;  // Controlled_Buffer controlled_buffer_13
  and and_15 (PUT, PUT_t, 1'b1);
  D_Flip_Flop d_ff_1 (.Q(INT), .preset(and_14_out), .reset(RET));  // open: D, clk, Qn
  assign STR_SYS_IN = GET_t ? GET_t : 1'bz;  // Controlled_Buffer controlled_buffer_14
  assign LOD_SYS_IN = MVG_t ? MVG_t : 1'bz;  // Controlled_Buffer controlled_buffer_15
  assign PSH = PSH_t ? PSH_t : 1'bz;  // Controlled_Buffer controlled_buffer_16
  assign POP = POP_t ? POP_t : 1'bz;  // Controlled_Buffer controlled_buffer_17
  assign STR_INS = PSH_t ? PSH_t : 1'bz;  // Controlled_Buffer controlled_buffer_18
  and and_16 (PNG, PNG_t, 1'b1);

  assign MVG = LOD_SYS_IN;
  assign STR_A = MVA;
  assign STR_B = MVB;

  // Other names for the same wires on the sheet: OP1[3:0] = IR_OUT[11:8]; JMP_ADR[7:0] = IR_OUT[7:0];
  //   OP3[3:0] = IR_OUT[3:0]; OP2[3:0] = IR_OUT[7:4]; OPCODE[3:0] = IR_OUT[15:12]
endmodule

module SYS_OUT (
  input  [15:0] SYS_OUT_IN,
  input  CLK,
  input  CLR,
  input  [2:0] SYS_OUT_ADR,
  input  PUT,
  output [15:0] SYS_OUT0,
  output [15:0] SYS_OUT1,
  output [15:0] SYS_OUT2,
  output [15:0] SYS_OUT3,
  output [15:0] SYS_OUT4,
  output [15:0] SYS_OUT5,
  output [15:0] SYS_OUT6,
  output [15:0] SYS_OUT7
);

  wire STR_SYS_OUT0, STR_SYS_OUT1, STR_SYS_OUT2, STR_SYS_OUT3, STR_SYS_OUT4, STR_SYS_OUT5, STR_SYS_OUT6,
       STR_SYS_OUT7;

  Decoder #(.select(3)) decoder_1 (
    .out0(STR_SYS_OUT0), .out1(STR_SYS_OUT1), .out2(STR_SYS_OUT2), .out3(STR_SYS_OUT3), .out4(STR_SYS_OUT4),
    .out5(STR_SYS_OUT5), .out6(STR_SYS_OUT6), .out7(STR_SYS_OUT7), .sel(SYS_OUT_ADR), .en(PUT));
  REG16 reg16_1 (.REG_IN(SYS_OUT_IN), .STR(STR_SYS_OUT0), .LOD(1'b1), .CLK(CLK), .CLR(CLR), .REG_OUT(SYS_OUT0));
  REG16 reg16_2 (.REG_IN(SYS_OUT_IN), .STR(STR_SYS_OUT1), .LOD(1'b1), .CLK(CLK), .CLR(CLR), .REG_OUT(SYS_OUT1));
  REG16 reg16_3 (.REG_IN(SYS_OUT_IN), .STR(STR_SYS_OUT2), .LOD(1'b1), .CLK(CLK), .CLR(CLR), .REG_OUT(SYS_OUT2));
  REG16 reg16_4 (.REG_IN(SYS_OUT_IN), .STR(STR_SYS_OUT3), .LOD(1'b1), .CLK(CLK), .CLR(CLR), .REG_OUT(SYS_OUT3));
  REG16 reg16_5 (.REG_IN(SYS_OUT_IN), .STR(STR_SYS_OUT4), .LOD(1'b1), .CLK(CLK), .CLR(CLR), .REG_OUT(SYS_OUT4));
  REG16 reg16_6 (.REG_IN(SYS_OUT_IN), .STR(STR_SYS_OUT5), .LOD(1'b1), .CLK(CLK), .CLR(CLR), .REG_OUT(SYS_OUT5));
  REG16 reg16_7 (.REG_IN(SYS_OUT_IN), .STR(STR_SYS_OUT6), .LOD(1'b1), .CLK(CLK), .CLR(CLR), .REG_OUT(SYS_OUT6));
  REG16 reg16_8 (.REG_IN(SYS_OUT_IN), .STR(STR_SYS_OUT7), .LOD(1'b1), .CLK(CLK), .CLR(CLR), .REG_OUT(SYS_OUT7));
endmodule

module SYS_IN (
  input  [15:0] SYS_IN_IN,
  input  STR_SYS_IN,
  input  LOD_SYS_IN,
  input  CLK,
  input  CLR,
  input  RET_IN,
  output [15:0] SYS_IN_OUT,
  output RET
);

  REG16 reg16_1 (.REG_IN(SYS_IN_IN), .STR(STR_SYS_IN), .LOD(LOD_SYS_IN), .CLK(CLK), .CLR(CLR), .REG_OUT(SYS_IN_OUT));

  assign RET = RET_IN;
endmodule

module REG16 (
  input  [15:0] REG_IN,
  input  STR,
  input  LOD,
  input  CLK,
  input  CLR,
  output [15:0] REG_OUT
);

  wire [15:0] register_1_q;

  Register #(.width(16)) register_1 (.D(REG_IN), .en(STR), .Q(register_1_q), .clk(CLK), .clr(CLR));
  assign REG_OUT = LOD ? register_1_q : 16'bz;  // Controlled_Buffer controlled_buffer_1
endmodule

module PC16 (
  input  [7:0] PC_IN,
  input  STR_PC,
  input  LOD_PC,
  input  EN_PC,
  input  CLK,
  input  CLR,
  output [15:0] PC_OUT
);

  wire controlled_buffer_1_out;
  wire [7:0] PC_q;
  wire [15:0] bit_extender_1_out;

  Counter PC (.load(STR_PC), .D(PC_IN), .Q(PC_q), .clk(controlled_buffer_1_out), .clr(CLR));  // open: count, carry, up
  assign controlled_buffer_1_out = EN_PC ? CLK : 1'bz;  // Controlled_Buffer controlled_buffer_1
  assign bit_extender_1_out = {{8{1'b0}}, PC_q};  // Bit_Extender bit_extender_1
  assign PC_OUT = LOD_PC ? bit_extender_1_out : 16'bz;  // Controlled_Buffer controlled_buffer_2
endmodule

module STK (
  input  PSH,
  input  POP,
  input  CLK,
  input  CLR,
  output [7:0] STK_ADR
);

  wire controlled_buffer_1_out, controlled_buffer_3_out, not_1_out;
  wire [7:0] adder_1_out, counter_1_q, not_2_out;

  assign controlled_buffer_1_out = PSH ? 1'b1 : 1'bz;  // Controlled_Buffer controlled_buffer_1
  assign controlled_buffer_1_out = POP ? 1'b0 : 1'bz;  // Controlled_Buffer controlled_buffer_2
  not not_1 (not_1_out, CLK);
  assign controlled_buffer_3_out = PSH ? CLK : 1'bz;  // Controlled_Buffer controlled_buffer_3
  assign controlled_buffer_3_out = POP ? not_1_out : 1'bz;  // Controlled_Buffer controlled_buffer_4
  Counter counter_1 (
    .Q(counter_1_q), .up(controlled_buffer_1_out), .clk(controlled_buffer_3_out), .clr(CLR));  // open: load, D, count, carry
  assign not_2_out = ~counter_1_q;  // NOT_Gate not_2, 8 bits wide
  assign STK_ADR = PSH ? not_2_out : 8'bz;  // Controlled_Buffer controlled_buffer_5
  Adder adder_1 (.a(not_2_out), .b(8'h1), .out(adder_1_out));  // open: cin, cout
  assign STK_ADR = POP ? adder_1_out : 8'bz;  // Controlled_Buffer controlled_buffer_6
endmodule

module NET_CRD (
  input  [15:0] NET_CRD_IN,
  input  STR_NET_CRD,
  input  CLK,
  output [15:0] NET_CRD_OUT
);

  REG16 reg16_1 (.REG_IN(NET_CRD_IN), .STR(STR_NET_CRD), .LOD(1'b1), .CLK(CLK), .REG_OUT(NET_CRD_OUT));  // open: CLR
endmodule

module IN_MEM_COMPUTE (
  output [15:0] ADD,
  output [15:0] SUB,
  output [15:0] MUL,
  output [15:0] DIV
);

  wire clock_1_out;

  Clock clock_1 (.out(clock_1_out));
  PRICSSOR1 pricssor1_1 (
    .CLK(clock_1_out), .SYS_OUT0(ADD), .SYS_OUT1(SUB), .SYS_OUT2(MUL), .SYS_OUT3(DIV));  // open: RET_IN, SYS_IN_IN, CLR, HLT, SYS_OUT4, SYS_OUT5, SYS_OUT6, SYS_OUT7, SYS_PRT, PNG, PUT
endmodule

module BRANCHING (
  output [15:0] CTR
);

  wire clock_1_out;

  Clock clock_1 (.out(clock_1_out));
  PRICSSOR1 pricssor1_1 (
    .CLK(clock_1_out), .SYS_OUT0(CTR));  // open: RET_IN, SYS_IN_IN, CLR, HLT, SYS_OUT1, SYS_OUT2, SYS_OUT3, SYS_OUT4, SYS_OUT5, SYS_OUT6, SYS_OUT7, SYS_PRT, PNG, PUT
endmodule

module INTERRUPTS (
  input  [15:0] USER_INPUT,
  input  ACK,
  output [15:0] USER_VAL
);

  wire clock_1_out;

  Clock clock_1 (.out(clock_1_out));
  PRICSSOR1 pricssor1_1 (
    .RET_IN(ACK), .SYS_IN_IN(USER_INPUT), .CLK(clock_1_out), .SYS_OUT0(USER_VAL));  // open: CLR, HLT, SYS_OUT1, SYS_OUT2, SYS_OUT3, SYS_OUT4, SYS_OUT5, SYS_OUT6, SYS_OUT7, SYS_PRT, PNG, PUT
endmodule

module MAC (
  output [15:0] out_1,
  output [15:0] out_2,
  output [15:0] out_3,
  output [15:0] out_4
);

  wire clock_1_out;

  Clock clock_1 (.out(clock_1_out));
  PRICSSOR1 pricssor1_1 (
    .CLK(clock_1_out), .SYS_OUT0(out_1), .SYS_OUT1(out_2), .SYS_OUT2(out_3), .SYS_OUT3(out_4));  // open: RET_IN, SYS_IN_IN, CLR, HLT, SYS_OUT4, SYS_OUT5, SYS_OUT6, SYS_OUT7, SYS_PRT, PNG, PUT
endmodule

module PARALLELIZATION (
  output [15:0] out_1,
  output [15:0] out_2
);

  wire clock_1_out, pricssor1_1_png, pricssor1_2_png;
  wire [15:0] net_crd_1_net_crd_out, net_crd_2_net_crd_out, pricssor1_1_sys_prt, pricssor1_2_sys_prt;

  Clock clock_1 (.out(clock_1_out));
  NET_CRD net_crd_1 (
    .NET_CRD_IN(pricssor1_2_sys_prt), .STR_NET_CRD(pricssor1_2_png), .CLK(clock_1_out),
    .NET_CRD_OUT(net_crd_1_net_crd_out));
  PRICSSOR1 pricssor1_1 (
    .RET_IN(pricssor1_2_png), .SYS_IN_IN(net_crd_1_net_crd_out), .CLK(clock_1_out), .SYS_OUT0(out_1),
    .SYS_PRT(pricssor1_1_sys_prt), .PNG(pricssor1_1_png));  // open: CLR, HLT, SYS_OUT1, SYS_OUT2, SYS_OUT3, SYS_OUT4, SYS_OUT5, SYS_OUT6, SYS_OUT7, PUT
  NET_CRD net_crd_2 (
    .NET_CRD_IN(pricssor1_1_sys_prt), .STR_NET_CRD(pricssor1_1_png), .CLK(clock_1_out),
    .NET_CRD_OUT(net_crd_2_net_crd_out));
  PRICSSOR1 pricssor1_2 (
    .RET_IN(pricssor1_1_png), .SYS_IN_IN(net_crd_2_net_crd_out), .CLK(clock_1_out), .SYS_OUT0(out_2),
    .SYS_PRT(pricssor1_2_sys_prt), .PNG(pricssor1_2_png));  // open: CLR, HLT, SYS_OUT1, SYS_OUT2, SYS_OUT3, SYS_OUT4, SYS_OUT5, SYS_OUT6, SYS_OUT7, PUT
endmodule

module BOX (
);

  PRICSSOR1 pricssor1_1 ();  // open: RET_IN, SYS_IN_IN, CLR, CLK, HLT, SYS_OUT0, SYS_OUT1, SYS_OUT2, SYS_OUT3, SYS_OUT4, SYS_OUT5, SYS_OUT6, SYS_OUT7, SYS_PRT, PNG, PUT
endmodule

module INT (
  input  CLK,
  input  CLR
);

  wire and_1_out, CLK_t, DEC, EXE, FET, HLT, INT, nand_1_out, not_1_out, SYS;
  wire [1:0] FDE_q;

  not not_1 (not_1_out, HLT);
  and and_1 (and_1_out, CLK, not_1_out);
  nand nand_1 (nand_1_out, DEC, INT);
  and and_2 (CLK_t, and_1_out, nand_1_out);
  Counter #(.max('h3), .trigger("falling"), .width(2)) FDE (
    .Q(FDE_q), .clk(CLK_t), .clr(CLR));  // open: load, D, count, carry, up
  Decoder #(.select(2)) decoder_1 (.out0(FET), .out1(DEC), .out2(EXE), .out3(SYS), .sel(FDE_q));  // open: en
endmodule

module RETasdf (
  input  RET
);

  wire and_1_out, and_2_out, and_3_out, and_4_out, and_5_out, INT, not_1_out, not_2_out, not_3_out,
       not_4_out, not_5_out, not_6_out, not_7_out, not_8_out, SYS;
  wire [15:0] IR_OUT, multiplexer_1_out;

  Multiplexer #(.width(16)) multiplexer_1 (.in0({16{1'b0}}), .in1(IR_OUT), .out(multiplexer_1_out), .sel(SYS));
  and and_1 (and_1_out, multiplexer_1_out[0], multiplexer_1_out[1], multiplexer_1_out[2], multiplexer_1_out[3]);
  not not_1 (not_1_out, multiplexer_1_out[4]);
  not not_2 (not_2_out, multiplexer_1_out[5]);
  not not_3 (not_3_out, multiplexer_1_out[6]);
  not not_4 (not_4_out, multiplexer_1_out[7]);
  and and_2 (and_2_out, multiplexer_1_out[8], multiplexer_1_out[9], multiplexer_1_out[10], multiplexer_1_out[11]);
  not not_5 (not_5_out, multiplexer_1_out[12]);
  not not_6 (not_6_out, multiplexer_1_out[13]);
  not not_7 (not_7_out, multiplexer_1_out[14]);
  not not_8 (not_8_out, multiplexer_1_out[15]);
  and and_3 (and_3_out, not_1_out, not_2_out, not_3_out, not_4_out);
  and and_4 (and_4_out, not_5_out, not_6_out, not_7_out, not_8_out);
  and and_5 (and_5_out, and_1_out, and_3_out, and_2_out, and_4_out);
  D_Flip_Flop d_ff_1 (.Q(INT), .preset(and_5_out), .reset(RET));  // open: D, clk, Qn
endmodule

module THANK_U (
);

  wire clock_1_out, pricssor1_1_put;
  wire [15:0] pricssor1_1_sys_out0;

  Clock clock_1 (.out(clock_1_out));
  PRICSSOR1 pricssor1_1 (
    .CLK(clock_1_out), .SYS_OUT0(pricssor1_1_sys_out0), .PUT(pricssor1_1_put));  // open: RET_IN, SYS_IN_IN, CLR, HLT, SYS_OUT1, SYS_OUT2, SYS_OUT3, SYS_OUT4, SYS_OUT5, SYS_OUT6, SYS_OUT7, SYS_PRT, PNG
  TTY tty_1 (.data(pricssor1_1_sys_out0[6:0]), .clk(clock_1_out), .we(pricssor1_1_put));  // open: clr
endmodule
