// Logisim project arch.circ as structural Verilog: 13 circuits, main circuit main
module main (
  input  CLR,
  output [7:0] out_2
);

  wire and_1_out, GLB_CLK_out, multiplexer_2_out, multiplexer_3_out, multiplexer_4_out, multiplexer_5_out,
       multiplexer_7_out, N0, N1, neuron_1_en_acc, neuron_1_en_alu, neuron_1_en_sub, neuron_1_hlt,
       neuron_1_ld_acc, neuron_1_ld_out, neuron_1_set_ack, neuron_2_en_acc, neuron_2_en_alu, neuron_2_en_sub,
       neuron_2_hlt, neuron_2_ld_acc, neuron_2_ld_out, neuron_2_set_ack, nor_1_out, not_1_out, or_1_out;
  wire [7:0] acc_1_acc_alu, multiplexer_6_out, neuron_1_tmp_out, neuron_1_wbus_out, neuron_2_tmp_out,
       neuron_2_wbus_out, outreg_1_outreg_out, WBUS;

  Clock GLB_CLK (.out(GLB_CLK_out));
  Counter counter_1 (.Q(out_2), .clk(and_1_out), .clr(CLR));  // open: load, D, count, carry, up
  and and_1 (and_1_out, GLB_CLK_out, nor_1_out);
  nor nor_1 (nor_1_out, neuron_1_hlt, neuron_2_hlt);
  not not_1 (not_1_out, and_1_out);
  or or_1 (or_1_out, neuron_1_set_ack, neuron_2_set_ack);
  T_Flip_Flop t_ff_1 (.clk(not_1_out), .T(or_1_out), .Q(N1), .Qn(N0));  // open: preset, reset
  NEURON neuron_1 (
    .CLK_N(not_1_out), .CLK(and_1_out), .EN_NEURON(N0), .CLR(CLR), .LD_ACC(neuron_1_ld_acc),
    .EN_ACC(neuron_1_en_acc), .TMP_OUT(neuron_1_tmp_out), .EN_ALU(neuron_1_en_alu), .EN_SUB(neuron_1_en_sub),
    .SET_ACK(neuron_1_set_ack), .LD_OUT(neuron_1_ld_out), .HLT(neuron_1_hlt), .WBUS_OUT(neuron_1_wbus_out));
  NEURON neuron_2 (
    .CLK_N(not_1_out), .CLK(and_1_out), .EN_NEURON(N1), .CLR(CLR), .LD_ACC(neuron_2_ld_acc),
    .EN_ACC(neuron_2_en_acc), .TMP_OUT(neuron_2_tmp_out), .EN_ALU(neuron_2_en_alu), .EN_SUB(neuron_2_en_sub),
    .SET_ACK(neuron_2_set_ack), .LD_OUT(neuron_2_ld_out), .HLT(neuron_2_hlt), .WBUS_OUT(neuron_2_wbus_out));
  Multiplexer #(.width(8)) multiplexer_1 (.in0(neuron_1_wbus_out), .in1(neuron_2_wbus_out), .out(WBUS), .sel(N1));
  Multiplexer multiplexer_2 (.in0(neuron_1_ld_acc), .in1(neuron_2_ld_acc), .out(multiplexer_2_out), .sel(N1));
  Multiplexer multiplexer_3 (.in0(neuron_1_en_acc), .in1(neuron_2_en_acc), .out(multiplexer_3_out), .sel(N1));
  Multiplexer multiplexer_4 (.in0(neuron_1_en_alu), .in1(neuron_2_en_alu), .out(multiplexer_4_out), .sel(N1));
  Multiplexer multiplexer_5 (.in0(neuron_1_en_sub), .in1(neuron_2_en_sub), .out(multiplexer_5_out), .sel(N1));
  Multiplexer #(.width(8)) multiplexer_6 (
    .in0(neuron_1_tmp_out), .in1(neuron_2_tmp_out), .out(multiplexer_6_out), .sel(N1));
  ACC acc_1 (
    .ACC_IN(WBUS), .LD_ACC(multiplexer_2_out), .EN_ACC(multiplexer_3_out), .CLK(GLB_CLK_out), .ACC_OUT(WBUS),
    .ACC_ALU(acc_1_acc_alu));
  Multiplexer multiplexer_7 (.in0(neuron_1_ld_out), .in1(neuron_2_ld_out), .out(multiplexer_7_out), .sel(N1));
  ALU alu_1 (
    .ACC_IN(acc_1_acc_alu), .TMP_IN(multiplexer_6_out), .EN_ALU(multiplexer_4_out),
    .EN_SUB(multiplexer_5_out), .ALU_OUT(WBUS));
  Hex_Digit_Display hex_digit_display_1 (.value(outreg_1_outreg_out[7:4]));  // open: dp
  Hex_Digit_Display hex_digit_display_2 (.value(outreg_1_outreg_out[3:0]));  // open: dp
  OUTREG outreg_1 (.OUTREG_IN(WBUS), .LD_OUT(multiplexer_7_out), .CLK(GLB_CLK_out), .OUTREG_OUT(outreg_1_outreg_out));
endmodule

module main_beautify (
  input  CLR,
  output [7:0] out_2
);

  wire ACK0, ACK1, and_1_out, CLK, ENACC0, ENACC1, ENALU0, ENALU1, ENSUB0, ENSUB1, HLT0, HLT1, LDACC0,
       LDACC1, LDOUT0, LDOUT1, multiplexer_1_out, multiplexer_2_out, multiplexer_4_out, multiplexer_5_out,
       multiplexer_6_out, N0, N1, nor_1_out, not_1_out, or_1_out;
  wire [3:0] outreg_1_outreg_out, outreg_1_outreg_out_2;
  wire [7:0] acc_1_acc_alu, multiplexer_3_out, TMP0, TMP1, WBUS, WBUS0, WBUS1;

  Clock GLB_CLK (.out(CLK));
  Counter counter_1 (.Q(out_2), .clk(and_1_out), .clr(CLR));  // open: load, D, count, carry, up
  nor nor_1 (nor_1_out, HLT0, HLT1);
  and and_1 (and_1_out, CLK, nor_1_out);
  Multiplexer multiplexer_1 (.in0(LDACC0), .in1(LDACC1), .out(multiplexer_1_out), .sel(N1));
  Multiplexer multiplexer_2 (.in0(ENACC0), .in1(ENACC1), .out(multiplexer_2_out), .sel(N1));
  Multiplexer #(.width(8)) multiplexer_3 (.in0(TMP0), .in1(TMP1), .out(multiplexer_3_out), .sel(N1));
  Multiplexer multiplexer_4 (.in0(ENALU0), .in1(ENALU1), .out(multiplexer_4_out), .sel(N1));
  Multiplexer multiplexer_5 (.in0(ENSUB0), .in1(ENSUB1), .out(multiplexer_5_out), .sel(N1));
  not not_1 (not_1_out, and_1_out);
  // Probe on WBUS
  T_Flip_Flop t_ff_1 (.clk(not_1_out), .T(or_1_out), .Q(N1), .Qn(N0));  // open: preset, reset
  or or_1 (or_1_out, ACK0, ACK1);
  ACC acc_1 (
    .ACC_IN(WBUS), .LD_ACC(multiplexer_1_out), .EN_ACC(multiplexer_2_out), .CLK(CLK), .ACC_OUT(WBUS),
    .ACC_ALU(acc_1_acc_alu));
  Multiplexer multiplexer_6 (.in0(LDOUT0), .in1(LDOUT1), .out(multiplexer_6_out), .sel(N1));
  ALU alu_1 (
    .ACC_IN(acc_1_acc_alu), .TMP_IN(multiplexer_3_out), .EN_ALU(multiplexer_4_out),
    .EN_SUB(multiplexer_5_out), .ALU_OUT(WBUS));
  NEURON neuron_1 (
    .CLK_N(not_1_out), .CLK(and_1_out), .EN_NEURON(N0), .CLR(CLR), .LD_ACC(LDACC0), .EN_ACC(ENACC0),
    .TMP_OUT(TMP0), .EN_ALU(ENALU0), .EN_SUB(ENSUB0), .SET_ACK(ACK0), .LD_OUT(LDOUT0), .HLT(HLT1),
    .WBUS_OUT(WBUS0));
  NEURON neuron_2 (
    .CLK_N(not_1_out), .CLK(and_1_out), .EN_NEURON(N1), .CLR(CLR), .LD_ACC(LDACC1), .EN_ACC(ENACC1),
    .TMP_OUT(TMP1), .EN_ALU(ENALU1), .EN_SUB(ENSUB1), .SET_ACK(ACK1), .LD_OUT(LDOUT1), .HLT(HLT0),
    .WBUS_OUT(WBUS1));
  Hex_Digit_Display hex_digit_display_1 (.value(outreg_1_outreg_out_2));  // open: dp
  Hex_Digit_Display hex_digit_display_2 (.value(outreg_1_outreg_out));  // open: dp
  OUTREG outreg_1 (
    .OUTREG_IN(WBUS), .LD_OUT(multiplexer_6_out), .CLK(CLK),
    .OUTREG_OUT({outreg_1_outreg_out_2, outreg_1_outreg_out}));
  Multiplexer #(.width(8)) multiplexer_7 (.in0(WBUS0), .in1(WBUS1), .out(WBUS), .sel(N1));
endmodule

module CONTROL (
  input  [2:0] RING_IN,
  input  [3:0] OPCODE,
  output INC_PC,
  output EN_PC,
  output LD_AR,
  output EN_AR,
  output EN_RAM,
  output LD_IR,
  output EN_IR,
  output SET_ACK,
  output LD_ACC,
  output EN_ACC,
  output LD_OUT,
  output LD_TMP,
  output EN_ALU,
  output EN_SUB,
  output HLT
);

  wire ADD, and_1_out, and_2_out, and_3_out, and_4_out, CYC4, CYC5, CYC6, decoder_1_out7, HLT_t, LDA,
       or_2_out, or_3_out, or_4_out, or_5_out, OUT_C, SUB;

  Decoder #(.select(3)) decoder_1 (
    .out1(EN_PC), .out2(INC_PC), .out3(EN_IR), .out4(CYC4), .out5(CYC5), .out6(CYC6), .out7(decoder_1_out7),
    .sel(RING_IN));  // open: out0, en
  Decoder #(.select(4)) decoder_2 (
    .out0(LDA), .out1(ADD), .out2(SUB), .out14(OUT_C), .out15(HLT_t), .sel(OPCODE));  // open: out3, out4, out5, out6, out7, out8, out9, out10, out11, out12, out13, en
  or or_1 (LD_AR, EN_PC, EN_IR);
  or or_2 (or_2_out, LDA, ADD, SUB);
  and and_1 (and_1_out, or_2_out, CYC4);
  or or_3 (or_3_out, LDA, OUT_C);
  or or_4 (or_4_out, ADD, SUB);
  or or_5 (or_5_out, ADD, SUB);
  or or_6 (EN_AR, INC_PC, and_1_out);
  and and_2 (and_2_out, or_3_out, CYC4);
  and and_3 (and_3_out, CYC5, or_4_out);
  and and_4 (and_4_out, LDA, CYC4);
  and and_5 (EN_ALU, CYC5, or_5_out);
  and and_6 (EN_SUB, CYC5, SUB);
  and and_7 (HLT, HLT_t, CYC4);
  or or_7 (SET_ACK, and_2_out, and_3_out);
  or or_8 (LD_ACC, and_4_out, EN_ALU);
  and and_8 (EN_ACC, CYC4, OUT_C);
  and and_9 (LD_TMP, CYC4, or_5_out);

  assign EN_RAM = EN_AR;
  assign LD_IR = INC_PC;
  assign LD_OUT = EN_ACC;

  // Other names for the same wires on the sheet: CYC1 = EN_PC; CYC2 = INC_PC; CYC3 = EN_IR
endmodule

module RING (
  input  EN_RING,
  input  CLK,
  input  SET_ACK,
  input  CLR,
  output [2:0] RING_OUT
);

  wire and_1_out, and_2_out, and_3_out, decoder_1_out0, decoder_1_out1, decoder_1_out2, decoder_1_out3,
       decoder_1_out4, decoder_1_out5, decoder_1_out6, not_1_out, or_1_out, or_2_out, or_3_out, or_4_out,
       undriven;
  wire [2:0] multiplexer_1_out;

  and and_1 (and_1_out, or_4_out, CLK, EN_RING);
  and and_2 (and_2_out, CLK, or_3_out);
  or or_1 (or_1_out, and_1_out, and_2_out);
  not not_1 (not_1_out, CLK);
  and and_3 (and_3_out, not_1_out, SET_ACK);
  Multiplexer #(.width(3)) multiplexer_1 (.in1(3'b001), .out(multiplexer_1_out), .sel(undriven));  // open: in0
  or or_2 (or_2_out, and_3_out, CLR);
  Counter #(.max('h5), .width(3)) counter_1 (
    .load(undriven), .D(multiplexer_1_out), .Q(RING_OUT), .clk(or_1_out), .clr(or_2_out));  // open: count, carry, up
  Decoder #(.select(3)) decoder_1 (
    .out0(decoder_1_out0), .out1(decoder_1_out1), .out2(decoder_1_out2), .out3(decoder_1_out3),
    .out4(decoder_1_out4), .out5(decoder_1_out5), .out6(decoder_1_out6), .sel(RING_OUT));  // open: out7, en
  or or_3 (or_3_out, decoder_1_out1, decoder_1_out2, decoder_1_out0);
  or or_4 (or_4_out, decoder_1_out4, decoder_1_out3, decoder_1_out5, decoder_1_out6);
endmodule

module ACC (
  input  [7:0] ACC_IN,
  input  LD_ACC,
  input  EN_ACC,
  input  CLK,
  output [7:0] ACC_OUT,
  output [7:0] ACC_ALU
);

  wire [7:0] multiplexer_1_out;

  Multiplexer #(.width(8)) multiplexer_1 (.in0(ACC_ALU), .in1(ACC_IN), .out(multiplexer_1_out), .sel(LD_ACC));
  Register #(.trigger("falling")) register_1 (.D(multiplexer_1_out), .Q(ACC_ALU), .clk(CLK));  // open: en, clr
  assign ACC_OUT = EN_ACC ? ACC_ALU : 8'bz;  // Controlled_Buffer controlled_buffer_1
endmodule

module RAM8x8 (
  input  EN_RAM,
  input  [2:0] ADDR_IN,
  output [7:0] RAM_OUT
);

  wire [7:0] ram_1_dout;

  RAM #(.addrWidth(3), .enables("line"), .\type ("nonvolatile")) ram_1 (
    .addr(ADDR_IN), .dout(ram_1_dout));  // open: we, clk, din
  assign RAM_OUT = EN_RAM ? ram_1_dout : 8'bz;  // Controlled_Buffer controlled_buffer_1
endmodule

module NEURON (
  input  CLK_N,
  input  CLK,
  input  EN_NEURON,
  input  CLR,
  output LD_ACC,
  output EN_ACC,
  output [7:0] TMP_OUT,
  output EN_ALU,
  output EN_SUB,
  output SET_ACK,
  output LD_OUT,
  output HLT,
  output [7:0] WBUS_OUT
);

  wire control_1_en_ar, control_1_en_ir, control_1_en_pc, control_1_en_ram, control_1_inc_pc,
       control_1_ld_ar, control_1_ld_ir, control_1_ld_tmp;
  wire [2:0] ar_1_ar_out, ring_1_ring_out;
  wire [3:0] OPCODE;
  wire [3:3] ir_1_addr_out;

  RING ring_1 (.EN_RING(EN_NEURON), .CLK(CLK), .SET_ACK(SET_ACK), .CLR(CLR), .RING_OUT(ring_1_ring_out));
  CONTROL control_1 (
    .RING_IN(ring_1_ring_out), .OPCODE(OPCODE), .INC_PC(control_1_inc_pc), .EN_PC(control_1_en_pc),
    .LD_AR(control_1_ld_ar), .EN_AR(control_1_en_ar), .EN_RAM(control_1_en_ram), .LD_IR(control_1_ld_ir),
    .EN_IR(control_1_en_ir), .SET_ACK(SET_ACK), .LD_ACC(LD_ACC), .EN_ACC(EN_ACC), .LD_OUT(LD_OUT),
    .LD_TMP(control_1_ld_tmp), .EN_ALU(EN_ALU), .EN_SUB(EN_SUB), .HLT(HLT));
  TMP tmp_1 (.TMP_IN(WBUS_OUT), .LD_TMP(control_1_ld_tmp), .CLK_N(CLK_N), .TMP_OUT(TMP_OUT));
  PC pc_1 (.EN_PC(control_1_en_pc), .INC_PC(control_1_inc_pc), .CLK_N(CLK_N), .CLR(CLR), .PC_OUT(WBUS_OUT[2:0]));
  AR ar_1 (
    .AR_IN(WBUS_OUT[2:0]), .LD_AR(control_1_ld_ar), .EN_AR(control_1_en_ar), .CLK_N(CLK_N),
    .AR_OUT(ar_1_ar_out));
  RAM8x8 ram8x8_1 (.EN_RAM(control_1_en_ram), .ADDR_IN(ar_1_ar_out), .RAM_OUT(WBUS_OUT));
  IR ir_1 (
    .IR_IN(WBUS_OUT), .LD_IR(control_1_ld_ir), .EN_IR(control_1_en_ir), .CLK_N(CLK_N),
    .ADDR_OUT({ir_1_addr_out[3], WBUS_OUT[2:0]}), .OPCODE(OPCODE));
  // Probe on WBUS_OUT

  // Other names for the same wires on the sheet: WBUS[7:0] = WBUS_OUT
endmodule

module IR (
  input  [7:0] IR_IN,
  input  LD_IR,
  input  EN_IR,
  input  CLK_N,
  output [3:0] ADDR_OUT,
  output [3:0] OPCODE
);

  wire [3:0] register_1_q;
  wire [7:0] multiplexer_1_out;

  Multiplexer #(.width(8)) multiplexer_1 (
    .in0({OPCODE, register_1_q}), .in1(IR_IN), .out(multiplexer_1_out), .sel(LD_IR));
  Register #(.trigger("falling")) register_1 (
    .D(multiplexer_1_out), .Q({OPCODE, register_1_q}), .clk(CLK_N));  // open: en, clr
  assign ADDR_OUT = EN_IR ? register_1_q : 4'bz;  // Controlled_Buffer controlled_buffer_1
endmodule

module AR (
  input  [2:0] AR_IN,
  input  LD_AR,
  input  EN_AR,
  input  CLK_N,
  output [2:0] AR_OUT
);

  wire [2:0] multiplexer_1_out, register_1_q;

  Multiplexer #(.width(3)) multiplexer_1 (.in0(register_1_q), .in1(AR_IN), .out(multiplexer_1_out), .sel(LD_AR));
  Register #(.trigger("falling"), .width(3)) register_1 (
    .D(multiplexer_1_out), .Q(register_1_q), .clk(CLK_N));  // open: en, clr
  assign AR_OUT = EN_AR ? register_1_q : 3'bz;  // Controlled_Buffer controlled_buffer_1
endmodule

module PC (
  input  EN_PC,
  input  INC_PC,
  input  CLK_N,
  input  CLR,
  output [2:0] PC_OUT
);

  wire and_1_out;
  wire [2:0] counter_1_q;

  Counter #(.max('h7), .ongoal("stay"), .trigger("falling"), .width(3)) counter_1 (
    .Q(counter_1_q), .clk(and_1_out), .clr(CLR));  // open: load, D, count, carry, up
  and and_1 (and_1_out, INC_PC, CLK_N);
  assign PC_OUT = EN_PC ? counter_1_q : 3'bz;  // Controlled_Buffer controlled_buffer_1
endmodule

module ALU (
  input  [7:0] ACC_IN,
  input  [7:0] TMP_IN,
  input  EN_ALU,
  input  EN_SUB,
  output [7:0] ALU_OUT
);

  wire [7:0] adder_1_out, multiplexer_1_out, subtractor_1_out;

  Adder adder_1 (.a(ACC_IN), .b(TMP_IN), .out(adder_1_out));  // open: cin, cout
  Subtractor subtractor_1 (.a(ACC_IN), .b(TMP_IN), .out(subtractor_1_out));  // open: bin, bout
  Multiplexer #(.width(8)) multiplexer_1 (
    .in0(adder_1_out), .in1(subtractor_1_out), .out(multiplexer_1_out), .sel(EN_SUB));
  assign ALU_OUT = EN_ALU ? multiplexer_1_out : 8'bz;  // Controlled_Buffer controlled_buffer_1
endmodule

module TMP (
  input  [7:0] TMP_IN,
  input  LD_TMP,
  input  CLK_N,
  output [7:0] TMP_OUT
);

  wire [7:0] multiplexer_1_out;

  Multiplexer #(.width(8)) multiplexer_1 (.in0(TMP_OUT), .in1(TMP_IN), .out(multiplexer_1_out), .sel(LD_TMP));
  Register #(.trigger("falling")) register_1 (.D(multiplexer_1_out), .Q(TMP_OUT), .clk(CLK_N));  // open: en, clr
endmodule

module OUTREG (
  input  [7:0] OUTREG_IN,
  input  LD_OUT,
  input  CLK,
  output [7:0] OUTREG_OUT
);

  wire [7:0] multiplexer_1_out;

  Multiplexer #(.width(8)) multiplexer_1 (.in0(OUTREG_OUT), .in1(OUTREG_IN), .out(multiplexer_1_out), .sel(LD_OUT));
  Register #(.trigger("falling")) register_1 (.D(multiplexer_1_out), .Q(OUTREG_OUT), .clk(CLK));  // open: en, clr
endmodule
